# Fritzing sketch CapstoneV2 (saved by Fritzing 0.9.4)
breadboards: 3

parts:
  Breadboard4 = Breadboard Split Power
  Breadboard5 = Breadboard Split Power
  Argon1 = Particle Argon
  WS2812B1 = WS2812B [package="DIP (Dual Inline) [THT]"]
  WS2812B2 = WS2812B [package="DIP (Dual Inline) [THT]"]
  M1 = BMP280
  Part1 = Adafruit MicroSD card breakout board [part_number="Adafruit #254"]
  DFRobot_DFPlayer_Mini1 = DFRobot DFPlayer Mini [part_number=DFR0299]
  S1 = Pushbutton [package="[THT]"]
  S2 = Pushbutton [package="[THT]"]
  R1 = PHOTOCELL [package=photocell-kit]  # not connected
  Part2 = MQ-131 breakout

nets:
  GND: Breadboard4.pin3Z, Breadboard4.pin20Z, Breadboard4.pin29Z, Breadboard5.pin3Z, Breadboard5.pin11Z, Argon1.GND, WS2812B1.GND, WS2812B2.GND, M1.GND, Part1.GND, DFRobot_DFPlayer_Mini1.GND-1, DFRobot_DFPlayer_Mini1.GND-2, S1.Pin_1, S1.Pin_2, S2.Pin_1, S2.Pin_2, Part2.GND
  5V: Breadboard4.pin4Y, Breadboard4.pin15Y, Breadboard4.pin17Y, Breadboard4.pin21Y, Breadboard4.pin29Y, Breadboard5.pin3Y, Breadboard5.pin12Y, Breadboard5.pin15Y, Breadboard5.pin17Y, Argon1.VUSB, WS2812B1.5V, WS2812B2.5V, M1.VIN, Part1.+3V3, DFRobot_DFPlayer_Mini1.VCC, Part2.VCC
  N1: Argon1.A0, WS2812B2.DI
  N2: Argon1.SCK, Part1.CLK
  N3: Argon1.MO, Part1.DI
  N4: Argon1.MI, Part1.DO
  N5: Argon1.RX, DFRobot_DFPlayer_Mini1.TX
  N6: Argon1.TX, DFRobot_DFPlayer_Mini1.RX
  N7: Argon1.SDA, M1.SDA
  N8: Argon1.SCL, M1.SCL
  N9: WS2812B1.DI, WS2812B2.DO
  N10: S1.Pin_3, S1.Pin_4
  N11: S2.Pin_3, S2.Pin_4

custom parts:
  Breadboard Split Power: A custom 6 pin per group power supply strip where the top row (ground) is all bussed together and the bottom row (+V) is split in two groups of 12 pins. This version is modified to be a loadable part and was rescaled to be on the standard 1px = 1thou grid with the size set in inches
  Particle Argon: The Argon is a powerful Wi-Fi enabled development board that can act as either a standalone Wi-Fi endpoint or Wi-Fi enabled gateway for Particle Mesh networks. It is based on the Nordic nRF52840 and has built-in battery charging circuitry so it’s easy to connect a Li-Po and deploy your local network in minutes. The Argon is great for connecting existing projects to the Particle Device Cloud or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
  WS2812B: Adafruit NeoPixel Breakout
  BMP280: Temperature Humidity Barometric presure Sensor, I2C
  Adafruit MicroSD card breakout board: Not just a simple breakout board, this microSD adapter goes the extra mile - designed for ease of use. Onboard 5v->3v regulator provides 150mA for power-hungry cards 3v level shifting means you can use this with ease on either 3v or 5v systems Uses a proper level shifting chip, not resistors: less problems, and faster read/write access Use 3 or 4 digital pins to read and write 2Gb+ of storage!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
  Pushbutton: A generic pushbutton.
  MQ-131 breakout: SKU: 101282
